// Logisim project e2547875 (solution).circ as structural Verilog: 1 circuit, main circuit main
module main (
  input  A1,
  input  A0,
  input  B1,
  input  B0,
  input  O3,
  input  O2,
  input  O1,
  input  O0,
  output S,
  output C,
  output Z,
  output P,
  output E,
  output G,
  output L,
  output L9,
  output L8,
  output L7,
  output L6,
  output L5,
  output L4,
  output L3,
  output L2,
  output L1,
  output L0
);

  wire and_1_out, and_2_out, and_3_out, nor_1_out, not_1_out, not_2_out, not_3_out, not_4_out, not_5_out,
       not_6_out, not_7_out, not_8_out, not_9_out, not_10_out, not_11_out, not_12_out, not_13_out,
       not_14_out, not_15_out, not_16_out, not_17_out, not_18_out, not_19_out, not_20_out, not_21_out,
       not_22_out, not_23_out, not_24_out, not_25_out, not_26_out, not_27_out, not_28_out, not_29_out,
       not_30_out, or_1_out, or_2_out, or_3_out, or_4_out, or_5_out, or_6_out, or_7_out, or_8_out, or_9_out,
       or_10_out, or_11_out, or_12_out, or_13_out, or_14_out, or_15_out, or_16_out, or_17_out, or_18_out,
       or_19_out, or_20_out, or_21_out, or_22_out, or_23_out, or_24_out, or_25_out, or_26_out, or_27_out,
       or_28_out, or_29_out, or_30_out, or_31_out, or_32_out, or_33_out, or_34_out, or_35_out, or_36_out,
       or_37_out, or_38_out, or_39_out, or_40_out, or_41_out, or_42_out, or_43_out, or_44_out, or_45_out,
       or_46_out, or_47_out, or_48_out, or_49_out, or_50_out, or_51_out, or_52_out, or_53_out, or_54_out,
       or_55_out, or_56_out, or_57_out, or_58_out, or_59_out, or_60_out, or_61_out, or_62_out, or_63_out,
       or_64_out, or_65_out, or_66_out, or_67_out, or_68_out, or_69_out, or_70_out, or_71_out, or_72_out,
       or_73_out, or_74_out, or_75_out, or_76_out, or_77_out, or_78_out, or_79_out, or_80_out, or_81_out,
       or_82_out, or_83_out, or_84_out, or_85_out, or_86_out, or_87_out, or_88_out, or_89_out, or_90_out,
       or_91_out, or_92_out, or_93_out, or_94_out, or_95_out, or_96_out, or_97_out, or_98_out, or_99_out,
       or_100_out, or_101_out, or_102_out, or_103_out, or_104_out, or_105_out, or_106_out, or_107_out,
       or_108_out, or_109_out, or_110_out, or_111_out, or_112_out, or_113_out, or_114_out, or_115_out,
       or_116_out, or_117_out, or_118_out, or_119_out, or_120_out, or_121_out, or_122_out, or_123_out;

  not not_1 (not_1_out, A1);
  // _3_to_8_decoder__74138 #(.Facing("east")) 3_to_8_decoder_74138_1: pin names not known; wires that end beside it: B0, B1, A0
  // _3_to_8_decoder__74138 #(.Facing("east")) 3_to_8_decoder_74138_2: pin names not known; wires that end beside it: B0, B1, A0, not_1_out, A1, 1'b0, 1'b0, 1'b0, 1'b0
  // NOT_Gate not_2 has open pins: in=open, out=not_2_out
  // NOT_Gate not_3 has open pins: in=open, out=not_3_out
  // NOT_Gate not_4 has open pins: in=open, out=not_4_out
  // NOT_Gate not_5 has open pins: in=open, out=not_5_out
  // NOT_Gate not_6 has open pins: in=open, out=not_6_out
  // NOT_Gate not_7 has open pins: in=open, out=not_7_out
  // NOT_Gate not_8 has open pins: in=open, out=not_8_out
  // NOT_Gate not_9 has open pins: in=open, out=not_9_out
  // NOT_Gate not_10 has open pins: in=open, out=not_10_out
  // NOT_Gate not_11 has open pins: in=open, out=not_11_out
  // NOT_Gate not_12 has open pins: in=open, out=not_12_out
  // NOT_Gate not_13 has open pins: in=open, out=not_13_out
  // NOT_Gate not_14 has open pins: in=open, out=not_14_out
  // NOT_Gate not_15 has open pins: in=open, out=not_15_out
  // NOT_Gate not_16 has open pins: in=open, out=not_16_out
  // NOT_Gate not_17 has open pins: in=open, out=not_17_out
  or or_1 (or_1_out, not_3_out, not_4_out);
  or or_2 (or_2_out, not_5_out, not_8_out);
  or or_3 (or_3_out, not_9_out, not_13_out);
  or or_4 (or_4_out, or_1_out, or_2_out);
  or or_5 (or_5_out, not_2_out, not_7_out);
  or or_6 (or_6_out, not_12_out, not_13_out);
  or or_7 (or_7_out, not_7_out, not_16_out);
  or or_8 (or_8_out, or_4_out, or_3_out);
  or or_9 (or_9_out, or_3_out, not_12_out);
  or or_10 (or_10_out, not_15_out, not_16_out);
  or or_11 (or_11_out, or_5_out, or_12_out);
  or or_12 (or_12_out, not_12_out, not_17_out);
  or or_13 (or_13_out, not_11_out, not_14_out);
  or or_14 (or_14_out, not_6_out, not_10_out);
  or or_15 (or_15_out, or_9_out, not_17_out);
  or or_16 (or_16_out, or_15_out, or_10_out);
  or or_17 (or_17_out, not_8_out, not_9_out);
  or or_18 (or_18_out, or_17_out, or_19_out);
  or or_19 (or_19_out, not_13_out, not_16_out);
  or or_20 (or_20_out, not_7_out, not_8_out);
  or or_21 (or_21_out, or_20_out, or_22_out);
  or or_22 (or_22_out, not_11_out, not_12_out);
  or or_23 (or_23_out, or_22_out, or_7_out);
  or or_24 (or_24_out, not_7_out, or_25_out);
  or or_25 (or_25_out, not_6_out, or_1_out);
  or or_26 (or_26_out, or_25_out, not_8_out);
  or or_27 (or_27_out, not_10_out, not_11_out);
  or or_28 (or_28_out, or_10_out, or_13_out);
  or or_29 (or_29_out, or_28_out, or_14_out);
  or or_30 (or_30_out, not_17_out, or_23_out);
  or or_31 (or_31_out, not_9_out, or_24_out);
  or or_32 (or_32_out, or_31_out, not_10_out);
  or or_33 (or_33_out, not_9_out, or_26_out);
  or or_34 (or_34_out, or_33_out, or_27_out);
  or or_35 (or_35_out, not_7_out, not_9_out);
  or or_36 (or_36_out, or_35_out, or_6_out);
  or or_37 (or_37_out, not_15_out, or_38_out);
  or or_38 (or_38_out, or_32_out, not_12_out);
  or or_39 (or_39_out, not_15_out, or_40_out);
  or or_40 (or_40_out, or_34_out, or_19_out);
  or or_41 (or_41_out, or_10_out, or_36_out);
  // _3_to_8_decoder__74138 #(.Facing("east")) 3_to_8_decoder_74138_3: pin names not known; wires that end beside it: O0, O1, O2, 1'b1, 1'b0, 1'b0
  or or_42 (or_42_out, not_6_out, or_1_out);
  or or_43 (or_43_out, not_9_out, not_10_out);
  or or_44 (or_44_out, or_25_out, not_7_out);
  or or_45 (or_45_out, not_10_out, not_12_out);
  not not_18 (not_18_out, O3);
  // NOT_Gate not_19 has open pins: in=open, out=not_19_out
  // NOT_Gate not_20 has open pins: in=open, out=not_20_out
  // NOT_Gate not_21 has open pins: in=open, out=not_21_out
  // NOT_Gate not_22 has open pins: in=open, out=not_22_out
  // NOT_Gate not_23 has open pins: in=open, out=not_23_out
  // NOT_Gate not_24 has open pins: in=open, out=not_24_out
  // NOT_Gate not_25 has open pins: in=open, out=not_25_out
  // NOT_Gate not_26 has open pins: in=open, out=not_26_out
  not not_27 (not_27_out, not_23_out);
  or or_46 (or_46_out, not_13_out, or_48_out);
  or or_47 (or_47_out, or_46_out, or_10_out);
  or or_48 (or_48_out, or_42_out, or_43_out);
  or or_49 (or_49_out, or_44_out, or_45_out);
  and and_1 (and_1_out, not_18_out, not_19_out);
  and and_2 (and_2_out, not_19_out, O3);
  not not_28 (not_28_out, not_22_out);
  not not_29 (not_29_out, not_20_out);
  not not_30 (not_30_out, not_24_out);
  assign S = not_23_out ? or_8_out : 1'bz;  // Controlled_Buffer controlled_buffer_1
  assign P = and_1_out ? or_18_out : 1'bz;  // Controlled_Buffer controlled_buffer_2
  assign C = not_22_out ? or_16_out : 1'bz;  // Controlled_Buffer controlled_buffer_3
  assign S = not_27_out ? 1'b0 : 1'bz;  // Controlled_Buffer controlled_buffer_4
  assign C = not_28_out ? 1'b0 : 1'bz;  // Controlled_Buffer controlled_buffer_5
  assign P = not_22_out ? or_37_out : 1'bz;  // Controlled_Buffer controlled_buffer_6
  assign P = not_20_out ? or_21_out : 1'bz;  // Controlled_Buffer controlled_buffer_7
  assign P = not_21_out ? or_30_out : 1'bz;  // Controlled_Buffer controlled_buffer_8
  assign P = not_23_out ? or_39_out : 1'bz;  // Controlled_Buffer controlled_buffer_9
  assign P = and_2_out ? or_49_out : 1'bz;  // Controlled_Buffer controlled_buffer_10
  assign P = not_25_out ? or_41_out : 1'bz;  // Controlled_Buffer controlled_buffer_11
  assign P = not_26_out ? or_47_out : 1'bz;  // Controlled_Buffer controlled_buffer_12
  assign P = not_24_out ? 1'b0 : 1'bz;  // Controlled_Buffer controlled_buffer_13
  or or_50 (or_50_out, not_13_out, not_16_out);
  assign E = not_24_out ? or_11_out : 1'bz;  // Controlled_Buffer controlled_buffer_14
  assign G = not_24_out ? or_29_out : 1'bz;  // Controlled_Buffer controlled_buffer_15
  assign E = not_30_out ? 1'b0 : 1'bz;  // Controlled_Buffer controlled_buffer_16
  nor nor_1 (nor_1_out, or_11_out, or_29_out);
  assign L = not_24_out ? nor_1_out : 1'bz;  // Controlled_Buffer controlled_buffer_17
  assign G = not_30_out ? 1'b0 : 1'bz;  // Controlled_Buffer controlled_buffer_18
  assign L9 = not_20_out ? not_17_out : 1'bz;  // Controlled_Buffer controlled_buffer_19
  assign L = not_30_out ? 1'b0 : 1'bz;  // Controlled_Buffer controlled_buffer_20
  assign L6 = not_22_out ? not_17_out : 1'bz;  // Controlled_Buffer controlled_buffer_21
  assign L6 = not_20_out ? or_50_out : 1'bz;  // Controlled_Buffer controlled_buffer_22
  assign L9 = not_29_out ? 1'b0 : 1'bz;  // Controlled_Buffer controlled_buffer_23
  or or_51 (or_51_out, not_21_out, and_1_out);
  or or_52 (or_52_out, or_51_out, not_23_out);
  or or_53 (or_53_out, or_52_out, not_24_out);
  or or_54 (or_54_out, or_53_out, not_25_out);
  assign L6 = or_56_out ? 1'b0 : 1'bz;  // Controlled_Buffer controlled_buffer_24
  or or_55 (or_55_out, or_54_out, not_26_out);
  or or_56 (or_56_out, or_55_out, and_2_out);
  assign L5 = not_22_out ? or_50_out : 1'bz;  // Controlled_Buffer controlled_buffer_25
  assign L5 = not_28_out ? 1'b0 : 1'bz;  // Controlled_Buffer controlled_buffer_26
  or or_57 (or_57_out, not_9_out, not_12_out);
  assign L4 = not_20_out ? not_12_out : 1'bz;  // Controlled_Buffer controlled_buffer_27
  assign L4 = and_3_out ? 1'b0 : 1'bz;  // Controlled_Buffer controlled_buffer_28
  and and_3 (and_3_out, not_28_out, not_29_out);
  or or_58 (or_58_out, not_15_out, or_57_out);
  assign L4 = not_22_out ? or_58_out : 1'bz;  // Controlled_Buffer controlled_buffer_29
  assign L3 = and_1_out ? 1'b0 : 1'bz;  // Controlled_Buffer controlled_buffer_30
  or or_59 (or_59_out, not_15_out, not_9_out);
  assign L3 = not_21_out ? not_15_out : 1'bz;  // Controlled_Buffer controlled_buffer_31
  assign L3 = not_22_out ? or_63_out : 1'bz;  // Controlled_Buffer controlled_buffer_32
  assign L3 = not_20_out ? or_59_out : 1'bz;  // Controlled_Buffer controlled_buffer_33
  or or_60 (or_60_out, not_8_out, not_5_out);
  or or_61 (or_61_out, not_14_out, not_11_out);
  or or_62 (or_62_out, not_14_out, not_5_out);
  assign L3 = not_23_out ? or_62_out : 1'bz;  // Controlled_Buffer controlled_buffer_34
  assign L3 = not_25_out ? not_17_out : 1'bz;  // Controlled_Buffer controlled_buffer_35
  assign L3 = not_24_out ? 1'b0 : 1'bz;  // Controlled_Buffer controlled_buffer_36
  or or_63 (or_63_out, or_60_out, or_61_out);
  or or_64 (or_64_out, not_9_out, or_63_out);
  assign L3 = and_2_out ? or_67_out : 1'bz;  // Controlled_Buffer controlled_buffer_37
  assign L3 = not_26_out ? or_63_out : 1'bz;  // Controlled_Buffer controlled_buffer_38
  or or_65 (or_65_out, not_15_out, or_66_out);
  or or_66 (or_66_out, not_13_out, or_64_out);
  or or_67 (or_67_out, not_17_out, or_68_out);
  or or_68 (or_68_out, not_16_out, or_65_out);
  assign L2 = and_1_out ? not_13_out : 1'bz;  // Controlled_Buffer controlled_buffer_39
  or or_69 (or_69_out, not_11_out, not_8_out);
  assign L2 = not_22_out ? or_70_out : 1'bz;  // Controlled_Buffer controlled_buffer_40
  assign L2 = not_20_out ? or_69_out : 1'bz;  // Controlled_Buffer controlled_buffer_41
  assign L2 = not_21_out ? not_11_out : 1'bz;  // Controlled_Buffer controlled_buffer_42
  or or_70 (or_70_out, not_10_out, or_71_out);
  or or_71 (or_71_out, not_7_out, not_4_out);
  assign L2 = not_23_out ? or_72_out : 1'bz;  // Controlled_Buffer controlled_buffer_43
  assign L2 = not_24_out ? 1'b0 : 1'bz;  // Controlled_Buffer controlled_buffer_44
  or or_72 (or_72_out, not_15_out, or_73_out);
  or or_73 (or_73_out, not_10_out, or_74_out);
  or or_74 (or_74_out, not_9_out, not_4_out);
  or or_75 (or_75_out, not_12_out, or_76_out);
  or or_76 (or_76_out, not_10_out, not_4_out);
  assign L2 = not_26_out ? or_82_out : 1'bz;  // Controlled_Buffer controlled_buffer_45
  assign L2 = and_2_out ? or_75_out : 1'bz;  // Controlled_Buffer controlled_buffer_46
  assign L2 = not_25_out ? or_77_out : 1'bz;  // Controlled_Buffer controlled_buffer_47
  or or_77 (or_77_out, not_16_out, or_78_out);
  or or_78 (or_78_out, not_13_out, not_12_out);
  or or_79 (or_79_out, not_10_out, or_80_out);
  or or_80 (or_80_out, not_9_out, not_4_out);
  assign L1 = not_20_out ? not_7_out : 1'bz;  // Controlled_Buffer controlled_buffer_48
  assign L1 = and_1_out ? or_85_out : 1'bz;  // Controlled_Buffer controlled_buffer_49
  or or_81 (or_81_out, not_9_out, not_8_out);
  or or_82 (or_82_out, not_15_out, or_79_out);
  or or_83 (or_83_out, not_12_out, not_7_out);
  or or_84 (or_84_out, or_83_out, not_16_out);
  assign L1 = not_22_out ? or_86_out : 1'bz;  // Controlled_Buffer controlled_buffer_50
  assign L1 = not_21_out ? or_87_out : 1'bz;  // Controlled_Buffer controlled_buffer_51
  assign L1 = not_23_out ? or_92_out : 1'bz;  // Controlled_Buffer controlled_buffer_52
  or or_85 (or_85_out, not_16_out, or_81_out);
  or or_86 (or_86_out, not_3_out, not_6_out);
  or or_87 (or_87_out, not_17_out, or_84_out);
  assign L1 = not_25_out ? or_95_out : 1'bz;  // Controlled_Buffer controlled_buffer_53
  assign L1 = not_24_out ? 1'b0 : 1'bz;  // Controlled_Buffer controlled_buffer_54
  or or_88 (or_88_out, not_7_out, not_9_out);
  or or_89 (or_89_out, or_86_out, not_8_out);
  or or_90 (or_90_out, or_89_out, not_11_out);
  or or_91 (or_91_out, or_90_out, not_13_out);
  or or_92 (or_92_out, or_91_out, not_16_out);
  assign L1 = not_26_out ? or_96_out : 1'bz;  // Controlled_Buffer controlled_buffer_55
  assign L1 = and_2_out ? or_100_out : 1'bz;  // Controlled_Buffer controlled_buffer_56
  or or_93 (or_93_out, not_3_out, not_6_out);
  or or_94 (or_94_out, or_93_out, not_13_out);
  or or_95 (or_95_out, or_88_out, not_15_out);
  or or_96 (or_96_out, or_94_out, not_16_out);
  or or_97 (or_97_out, not_3_out, not_4_out);
  or or_98 (or_98_out, or_97_out, not_5_out);
  or or_99 (or_99_out, not_3_out, not_6_out);
  or or_100 (or_100_out, or_99_out, not_7_out);
  assign L0 = and_1_out ? or_105_out : 1'bz;  // Controlled_Buffer controlled_buffer_57
  assign L0 = not_21_out ? or_116_out : 1'bz;  // Controlled_Buffer controlled_buffer_58
  assign L0 = not_20_out ? or_111_out : 1'bz;  // Controlled_Buffer controlled_buffer_59
  or or_101 (or_101_out, not_15_out, not_17_out);
  or or_102 (or_102_out, not_12_out, or_101_out);
  or or_103 (or_103_out, not_11_out, or_102_out);
  or or_104 (or_104_out, or_98_out, not_7_out);
  or or_105 (or_105_out, or_104_out, or_103_out);
  assign L0 = not_22_out ? not_2_out : 1'bz;  // Controlled_Buffer controlled_buffer_60
  assign L0 = not_23_out ? or_118_out : 1'bz;  // Controlled_Buffer controlled_buffer_61
  assign L0 = not_24_out ? 1'b0 : 1'bz;  // Controlled_Buffer controlled_buffer_62
  or or_106 (or_106_out, not_2_out, not_3_out);
  or or_107 (or_107_out, not_6_out, not_10_out);
  or or_108 (or_108_out, not_5_out, or_107_out);
  or or_109 (or_109_out, or_106_out, not_4_out);
  or or_110 (or_110_out, or_109_out, or_108_out);
  or or_111 (or_111_out, not_14_out, or_110_out);
  assign L0 = not_25_out ? or_120_out : 1'bz;  // Controlled_Buffer controlled_buffer_63
  assign L0 = not_26_out ? or_118_out : 1'bz;  // Controlled_Buffer controlled_buffer_64
  or or_112 (or_112_out, not_2_out, not_7_out);
  or or_113 (or_113_out, not_8_out, not_9_out);
  or or_114 (or_114_out, or_112_out, not_12_out);
  or or_115 (or_115_out, or_98_out, or_113_out);
  or or_116 (or_116_out, or_115_out, not_13_out);
  assign L0 = and_2_out ? not_2_out : 1'bz;  // Controlled_Buffer controlled_buffer_65
  or or_117 (or_117_out, or_109_out, not_5_out);
  or or_118 (or_118_out, or_114_out, not_17_out);
  or or_119 (or_119_out, or_117_out, not_6_out);
  or or_120 (or_120_out, or_119_out, or_123_out);
  or or_121 (or_121_out, not_11_out, not_14_out);
  or or_122 (or_122_out, not_10_out, or_121_out);
  or or_123 (or_123_out, not_8_out, or_122_out);

  assign L7 = 1'b0;
  assign L8 = 1'b0;
  assign Z = L0;
endmodule
